# Fritzing sketch Q_Behave_RGB_Led (saved by Fritzing 0.8.7b)
breadboards: 1

parts:
  Procesor = Arduino Uno (Rev3)
  Reward = Pushbutton [package="[THT]"]
  Button3 = Pushbutton [package="[THT]"]
  Button2 = Pushbutton [package="[THT]"]
  Button1 = Pushbutton [package="[THT]"]
  RGB_Led = RGB LED (com. anode, rbg) [package="5 mm [THT]"]
  R4 = Resistor [tolerance=±5% resistance=10k package=THT]
  R3 = Resistor [tolerance=±5% resistance=10k package=THT]
  R1 = Resistor [tolerance=±5% resistance=10k package=THT]
  R2 = Resistor [tolerance=±5% resistance=10k package=THT]

nets:
  N1: Procesor.A0, Button1.Pin_1, Button1.Pin_2, R2.Pin_0
  N2: Procesor.A1, Button2.Pin_1, Button2.Pin_2, R1.Pin_0
  N3: Procesor.A2, Button3.Pin_1, Button3.Pin_2, R3.Pin_0
  N4: Procesor.A3, Reward.Pin_1, Reward.Pin_2, R4.Pin_0
  N5: Procesor.D9_PWM, RGB_Led.red_cathode
  N6: Procesor.D10_PWM/SS, RGB_Led.green_cathode
  N7: Procesor.D11_PWM/MOSI, RGB_Led.blue_cathode
  N8: Procesor.GND, RGB_Led.common_anode, R4.Pin_1, R3.Pin_1, R1.Pin_1, R2.Pin_1
  N9: Procesor.3V3, Reward.Pin_3, Reward.Pin_4, Button3.Pin_3, Button3.Pin_4, Button2.Pin_3, Button2.Pin_4, Button1.Pin_3, Button1.Pin_4
