# Fritzing sketch Q_Behave_Single_Button (saved by Fritzing 0.8.7b)
breadboards: 1

parts:
  Procesor = Arduino Uno (Rev3)
  Button = Pushbutton [package="[THT]"]
  RGB_Led = RGB LED (com. anode, rbg) [package="5 mm [THT]"]
  R1 = Resistor [tolerance=±5% resistance=10k package=THT]

nets:
  N1: Procesor.A0, Button.Pin_1, Button.Pin_2, R1.Pin_0
  N2: Procesor.D9_PWM, RGB_Led.red_cathode
  N3: Procesor.D10_PWM/SS, RGB_Led.green_cathode
  N4: Procesor.D11_PWM/MOSI, RGB_Led.blue_cathode
  N5: Procesor.GND, RGB_Led.common_anode, R1.Pin_1
  N6: Procesor.3V3, Button.Pin_3, Button.Pin_4
